# Fritzing sketch ArduSpi (saved by Fritzing 0.7.12b)
breadboards: 1

parts:
  Slave-0 = Arduino Micro
  Slave-1 = Arduino Micro
  Master = Arduino

nets:
  N1: Slave-0.TX, Slave-1.TX, Master.D0RX
  N2: Slave-0.RX, Slave-1.RX, Master.D1TX
  GND: Slave-0.GND, Slave-1.GND, Master.GND
  N3: Slave-0.D10, Master.D2
  N4: Slave-0.D11, Master.D3
  N5: Slave-1.D10, Master.D4
  N6: Slave-1.D11, Master.D5

custom parts:
  Arduino Micro: Arduino Micro Microcontroller
